// Digital circuit alu.dig as structural Verilog
module alu (
  input  [7:0] BUS,
  input  [7:0] REG_AINT,
  input  ALU_S3,
  input  ALU_S2,
  input  ALU_S1,
  input  ALU_S0,
  input  ALU_M,
  input  nALU_OUT,
  input  VCC,
  input  GND,
  input  clk,
  input  ALU_BIN,
  input  FR_IN,
  output ZF,
  output CF,
  output NF,
  output VF
);

  wire _74181_1_pin9, _74181_1_pin10, _74181_1_pin11, _74181_2_pin7, _74181_2_pin9, _74181_2_pin10,
       _74181_2_pin11, _74245_1_pin5, _74245_1_pin9, _74573_1_pin11, _74573_1_pin12, _74573_1_pin13,
       _74573_1_pin14, _74573_1_pin15, _74573_1_pin16, _74573_1_pin17, _74573_1_pin18, _74573_1_pin19,
       _74573_2_pin11, and_2_out, and_3_out, and_4_out, and_5_out, bussplitter_1_d0, bussplitter_1_d1,
       bussplitter_1_d2, bussplitter_1_d3, bussplitter_1_d4, bussplitter_1_d5, bussplitter_1_d6,
       bussplitter_1_d7, bussplitter_2_d0, bussplitter_2_d1, bussplitter_2_d2, bussplitter_2_d3,
       bussplitter_2_d4, bussplitter_2_d5, bussplitter_2_d6, bussplitter_2_d7, nor_1_out, nor_2_out,
       nor_3_out, nor_4_out, not_1_out, not_2_out, undriven, xor_1_out, xor_2_out;

  BusSplitter #(.Bits(8)) bussplitter_1 (
    .D(BUS), .OE(nALU_OUT), .D0(bussplitter_1_d0), .D1(bussplitter_1_d1), .D2(bussplitter_1_d2),
    .D3(bussplitter_1_d3), .D4(bussplitter_1_d4), .D5(bussplitter_1_d5), .D6(bussplitter_1_d6),
    .D7(bussplitter_1_d7));
  _74573 _74573_1 (
    .pin1(GND), .pin2(bussplitter_1_d0), .pin3(bussplitter_1_d1), .pin4(bussplitter_1_d2),
    .pin5(bussplitter_1_d3), .pin6(bussplitter_1_d4), .pin7(bussplitter_1_d5), .pin8(bussplitter_1_d6),
    .pin9(bussplitter_1_d7), .pin10(GND), .pin11(_74573_1_pin11), .pin12(_74573_1_pin12),
    .pin13(_74573_1_pin13), .pin14(_74573_1_pin14), .pin15(_74573_1_pin15), .pin16(_74573_1_pin16),
    .pin17(_74573_1_pin17), .pin18(_74573_1_pin18), .pin19(_74573_1_pin19), .pin20(VCC));
  and and_1 (_74573_1_pin11, ALU_BIN, clk);
  BusSplitter #(.Bits(8)) bussplitter_2 (
    .D(REG_AINT), .OE(VCC), .D0(bussplitter_2_d0), .D1(bussplitter_2_d1), .D2(bussplitter_2_d2),
    .D3(bussplitter_2_d3), .D4(bussplitter_2_d4), .D5(bussplitter_2_d5), .D6(bussplitter_2_d6),
    .D7(bussplitter_2_d7));
  LED led_1 (.in(_74573_1_pin19));
  LED led_2 (.in(_74573_1_pin18));
  LED led_3 (.in(_74573_1_pin17));
  LED led_4 (.in(_74573_1_pin16));
  LED led_5 (.in(_74573_1_pin15));
  LED led_6 (.in(_74573_1_pin14));
  LED led_7 (.in(_74573_1_pin13));
  LED led_8 (.in(_74573_1_pin12));
  PowerSupply powersupply_1 (.VDD(VCC), .GND(GND));
  _74181 _74181_1 (
    .pin1(_74573_1_pin19), .pin2(bussplitter_2_d0), .pin3(ALU_S3), .pin4(ALU_S2), .pin5(ALU_S1),
    .pin6(ALU_S0), .pin7(VCC), .pin8(ALU_M), .pin9(_74181_1_pin9), .pin10(_74181_1_pin10),
    .pin11(_74181_1_pin11), .pin12(GND));  // open: pin13, pin14, pin15, pin16, pin17, pin18, pin19, pin20, pin21, pin22, pin23, pin24
  _74181 _74181_2 (
    .pin1(_74573_1_pin15), .pin2(bussplitter_2_d4), .pin3(ALU_S3), .pin4(ALU_S2), .pin5(ALU_S1),
    .pin6(ALU_S0), .pin7(_74181_2_pin7), .pin8(ALU_M), .pin9(_74181_2_pin9), .pin10(_74181_2_pin10),
    .pin11(_74181_2_pin11), .pin12(GND));  // open: pin13, pin14, pin15, pin16, pin17, pin18, pin19, pin20, pin21, pin22, pin23, pin24
  xor xor_1 (xor_1_out, _74245_1_pin9, bussplitter_2_d7);
  xor xor_2 (xor_2_out, _74573_1_pin12, bussplitter_2_d7);
  and and_2 (and_2_out, xor_1_out, not_1_out);
  not not_1 (not_1_out, xor_2_out);
  LED led_9 (.in(_74245_1_pin9));
  LED led_10 (.in(_74181_2_pin11));
  LED led_11 (.in(_74181_2_pin10));
  LED led_12 (.in(_74181_2_pin9));
  LED led_13 (.in(_74245_1_pin5));
  LED led_14 (.in(_74181_1_pin11));
  LED led_15 (.in(_74181_1_pin10));
  LED led_16 (.in(_74181_1_pin9));
  nor nor_1 (nor_1_out, _74181_1_pin9, _74181_1_pin10);
  nor nor_2 (nor_2_out, _74181_1_pin11, _74245_1_pin5);
  nor nor_3 (nor_3_out, _74181_2_pin9, _74181_2_pin10);
  nor nor_4 (nor_4_out, _74181_2_pin11, _74245_1_pin9);
  _74245 _74245_1 (
    .pin1(VCC), .pin2(_74181_1_pin9), .pin3(_74181_1_pin10), .pin4(_74181_1_pin11), .pin5(_74245_1_pin5),
    .pin6(_74181_2_pin9), .pin7(_74181_2_pin10), .pin8(_74181_2_pin11), .pin9(_74245_1_pin9), .pin10(GND),
    .pin11(bussplitter_1_d7), .pin12(bussplitter_1_d6), .pin13(bussplitter_1_d5), .pin14(bussplitter_1_d4),
    .pin15(bussplitter_1_d3), .pin16(bussplitter_1_d2), .pin17(bussplitter_1_d1), .pin18(bussplitter_1_d0),
    .pin19(nALU_OUT), .pin20(VCC));
  and and_3 (and_3_out, nor_1_out, nor_2_out);
  and and_4 (and_4_out, nor_3_out, nor_4_out);
  and and_5 (and_5_out, and_3_out, and_4_out);
  LED led_17 (.in(and_2_out));
  not not_2 (not_2_out, undriven);
  LED led_18 (.in(not_2_out));
  LED led_19 (.in(_74245_1_pin9));
  _74573 _74573_2 (
    .pin1(GND), .pin2(and_5_out), .pin3(not_2_out), .pin4(_74245_1_pin9), .pin5(and_2_out), .pin6(GND),
    .pin7(GND), .pin8(GND), .pin9(GND), .pin10(GND), .pin11(_74573_2_pin11), .pin16(VF), .pin17(NF),
    .pin18(CF), .pin19(ZF), .pin20(VCC));  // open: pin12, pin13, pin14, pin15
  LED led_20 (.in(and_5_out));
  and and_6 (_74573_2_pin11, FR_IN, clk);

  // Notes on the sheet:
  //   nALU_OUT: default 1
  //   VCC: default 1
  //   V
  //   N
  //   C
  //   Z
endmodule
