// Digital circuit register_h_l.dig as structural Verilog
module register_h_l (
  input  [7:0] BUS,
  input  nDEC_H,
  input  REG_LIN,
  input  REG_HIN,
  input  RST,
  input  VCC,
  input  GND,
  input  nREG_LOUT,
  input  nREG_HOUT,
  input  nPAIR_HLOUT,
  input  nINC_H,
  input  CLK,
  output [15:0] ADDR_BUS,
  output [15:0] REG_HLINT
);

  wire _74193_1_pin12, _74193_1_pin13, _74193_2_pin12, _74193_2_pin13, _74193_3_pin12, _74193_3_pin13,
       _74245_3_pin11, _74245_3_pin12, _74245_3_pin13, _74245_3_pin14, _74245_3_pin15, _74245_3_pin16,
       _74245_3_pin17, _74245_3_pin18, _74245_4_pin11, _74245_4_pin12, _74245_4_pin13, _74245_4_pin14,
       _74245_4_pin15, _74245_4_pin16, _74245_4_pin17, _74245_4_pin18, and_1_out, bussplitter_1_d0,
       bussplitter_1_d1, bussplitter_1_d2, bussplitter_1_d3, bussplitter_1_d4, bussplitter_1_d5,
       bussplitter_1_d6, bussplitter_1_d7, nand_1_out, nand_2_out;

  and and_1 (and_1_out, nREG_LOUT, nREG_HOUT);
  BusSplitter #(.Bits(8)) bussplitter_1 (
    .D(BUS), .OE(and_1_out), .D0(bussplitter_1_d0), .D1(bussplitter_1_d1), .D2(bussplitter_1_d2),
    .D3(bussplitter_1_d3), .D4(bussplitter_1_d4), .D5(bussplitter_1_d5), .D6(bussplitter_1_d6),
    .D7(bussplitter_1_d7));
  nand nand_1 (nand_1_out, REG_LIN, CLK);
  nand nand_2 (nand_2_out, CLK, REG_HIN);
  PowerSupply powersupply_1 (.VDD(VCC), .GND(GND));
  _74193 _74193_1 (
    .pin1(bussplitter_1_d1), .pin2(REG_HLINT[1]), .pin3(REG_HLINT[0]), .pin4(nDEC_H), .pin5(nINC_H),
    .pin6(REG_HLINT[2]), .pin7(REG_HLINT[3]), .pin8(GND), .pin9(bussplitter_1_d3), .pin10(bussplitter_1_d2),
    .pin11(nand_1_out), .pin12(_74193_1_pin12), .pin13(_74193_1_pin13), .pin14(RST),
    .pin15(bussplitter_1_d0), .pin16(VCC));
  _74193 _74193_2 (
    .pin1(bussplitter_1_d5), .pin2(REG_HLINT[5]), .pin3(REG_HLINT[4]), .pin4(_74193_1_pin13),
    .pin5(_74193_1_pin12), .pin6(REG_HLINT[6]), .pin7(REG_HLINT[7]), .pin8(GND), .pin9(bussplitter_1_d7),
    .pin10(bussplitter_1_d6), .pin11(nand_1_out), .pin12(_74193_2_pin12), .pin13(_74193_2_pin13),
    .pin14(RST), .pin15(bussplitter_1_d4), .pin16(VCC));
  _74193 _74193_3 (
    .pin1(bussplitter_1_d1), .pin2(REG_HLINT[9]), .pin3(REG_HLINT[8]), .pin4(_74193_2_pin13),
    .pin5(_74193_2_pin12), .pin6(REG_HLINT[10]), .pin7(REG_HLINT[11]), .pin8(GND), .pin9(bussplitter_1_d3),
    .pin10(bussplitter_1_d2), .pin11(nand_2_out), .pin12(_74193_3_pin12), .pin13(_74193_3_pin13),
    .pin14(RST), .pin15(bussplitter_1_d0), .pin16(VCC));
  _74193 _74193_4 (
    .pin1(bussplitter_1_d5), .pin2(REG_HLINT[13]), .pin3(REG_HLINT[12]), .pin4(_74193_3_pin13),
    .pin5(_74193_3_pin12), .pin6(REG_HLINT[14]), .pin7(REG_HLINT[15]), .pin8(GND), .pin9(bussplitter_1_d7),
    .pin10(bussplitter_1_d6), .pin11(nand_2_out), .pin14(RST), .pin15(bussplitter_1_d4), .pin16(VCC));  // open: pin12, pin13
  LED led_1 (.in(REG_HLINT[15]));
  LED led_2 (.in(REG_HLINT[14]));
  LED led_3 (.in(REG_HLINT[13]));
  LED led_4 (.in(REG_HLINT[12]));
  LED led_5 (.in(REG_HLINT[11]));
  LED led_6 (.in(REG_HLINT[10]));
  LED led_7 (.in(REG_HLINT[9]));
  LED led_8 (.in(REG_HLINT[8]));
  LED led_9 (.in(REG_HLINT[7]));
  LED led_10 (.in(REG_HLINT[6]));
  LED led_11 (.in(REG_HLINT[5]));
  LED led_12 (.in(REG_HLINT[4]));
  LED led_13 (.in(REG_HLINT[3]));
  LED led_14 (.in(REG_HLINT[2]));
  LED led_15 (.in(REG_HLINT[1]));
  LED led_16 (.in(REG_HLINT[0]));
  _74245 _74245_1 (
    .pin1(VCC), .pin2(REG_HLINT[0]), .pin3(REG_HLINT[1]), .pin4(REG_HLINT[2]), .pin5(REG_HLINT[3]),
    .pin6(REG_HLINT[4]), .pin7(REG_HLINT[5]), .pin8(REG_HLINT[6]), .pin9(REG_HLINT[7]), .pin10(GND),
    .pin11(bussplitter_1_d7), .pin12(bussplitter_1_d6), .pin13(bussplitter_1_d5), .pin14(bussplitter_1_d4),
    .pin15(bussplitter_1_d3), .pin16(bussplitter_1_d2), .pin17(bussplitter_1_d1), .pin18(bussplitter_1_d0),
    .pin19(nREG_LOUT), .pin20(VCC));
  _74245 _74245_2 (
    .pin1(VCC), .pin2(REG_HLINT[8]), .pin3(REG_HLINT[9]), .pin4(REG_HLINT[10]), .pin5(REG_HLINT[11]),
    .pin6(REG_HLINT[12]), .pin7(REG_HLINT[13]), .pin8(REG_HLINT[14]), .pin9(REG_HLINT[15]), .pin10(GND),
    .pin11(bussplitter_1_d7), .pin12(bussplitter_1_d6), .pin13(bussplitter_1_d5), .pin14(bussplitter_1_d4),
    .pin15(bussplitter_1_d3), .pin16(bussplitter_1_d2), .pin17(bussplitter_1_d1), .pin18(bussplitter_1_d0),
    .pin19(nREG_HOUT), .pin20(VCC));
  _74245 _74245_3 (
    .pin1(VCC), .pin2(REG_HLINT[0]), .pin3(REG_HLINT[1]), .pin4(REG_HLINT[2]), .pin5(REG_HLINT[3]),
    .pin6(REG_HLINT[4]), .pin7(REG_HLINT[5]), .pin8(REG_HLINT[6]), .pin9(REG_HLINT[7]), .pin10(GND),
    .pin11(_74245_3_pin11), .pin12(_74245_3_pin12), .pin13(_74245_3_pin13), .pin14(_74245_3_pin14),
    .pin15(_74245_3_pin15), .pin16(_74245_3_pin16), .pin17(_74245_3_pin17), .pin18(_74245_3_pin18),
    .pin19(nPAIR_HLOUT), .pin20(VCC));
  _74245 _74245_4 (
    .pin1(VCC), .pin2(REG_HLINT[8]), .pin3(REG_HLINT[9]), .pin4(REG_HLINT[10]), .pin5(REG_HLINT[11]),
    .pin6(REG_HLINT[12]), .pin7(REG_HLINT[13]), .pin8(REG_HLINT[14]), .pin9(REG_HLINT[15]), .pin10(GND),
    .pin11(_74245_4_pin11), .pin12(_74245_4_pin12), .pin13(_74245_4_pin13), .pin14(_74245_4_pin14),
    .pin15(_74245_4_pin15), .pin16(_74245_4_pin16), .pin17(_74245_4_pin17), .pin18(_74245_4_pin18),
    .pin19(nPAIR_HLOUT), .pin20(VCC));
  BusSplitter #(.Bits(16)) bussplitter_2 (
    .D(ADDR_BUS), .OE(GND), .D0(_74245_3_pin18), .D1(_74245_3_pin17), .D2(_74245_3_pin16),
    .D3(_74245_3_pin15), .D4(_74245_3_pin14), .D5(_74245_3_pin13), .D6(_74245_3_pin12), .D7(_74245_3_pin11),
    .D8(_74245_4_pin18), .D9(_74245_4_pin17), .D10(_74245_4_pin16), .D11(_74245_4_pin15),
    .D12(_74245_4_pin14), .D13(_74245_4_pin13), .D14(_74245_4_pin12), .D15(_74245_4_pin11));

  // Notes on the sheet:
  //   nDEC_H: default 1
  //   VCC: default 1
  //   nREG_LOUT: default 1
  //   nREG_HOUT: default 1
  //   nPAIR_HLOUT: default 1
  //   nINC_H: default 1
endmodule
