// Digital circuit stack_pointer.dig as structural Verilog
module stack_pointer (
  input  [7:0] BUS,
  input  nDEC_SP,
  input  SP_LIN,
  input  SP_HIN,
  input  RST,
  input  VCC,
  input  GND,
  input  nSP_OUT,
  input  nINC_SP,
  input  CLK,
  output [15:0] ADDR_BUS,
  output [15:0] SP_INT
);

  wire _74193_1_pin12, _74193_1_pin13, _74193_2_pin12, _74193_2_pin13, _74193_3_pin12, _74193_3_pin13,
       _74245_1_pin11, _74245_1_pin12, _74245_1_pin13, _74245_1_pin14, _74245_1_pin15, _74245_1_pin16,
       _74245_1_pin17, _74245_1_pin18, _74245_2_pin11, _74245_2_pin12, _74245_2_pin13, _74245_2_pin14,
       _74245_2_pin15, _74245_2_pin16, _74245_2_pin17, _74245_2_pin18, bussplitter_1_d0, bussplitter_1_d1,
       bussplitter_1_d2, bussplitter_1_d3, bussplitter_1_d4, bussplitter_1_d5, bussplitter_1_d6,
       bussplitter_1_d7, nand_1_out, nand_2_out;

  BusSplitter #(.Bits(8)) bussplitter_1 (
    .D(BUS), .OE(VCC), .D0(bussplitter_1_d0), .D1(bussplitter_1_d1), .D2(bussplitter_1_d2),
    .D3(bussplitter_1_d3), .D4(bussplitter_1_d4), .D5(bussplitter_1_d5), .D6(bussplitter_1_d6),
    .D7(bussplitter_1_d7));
  nand nand_1 (nand_1_out, SP_LIN, CLK);
  nand nand_2 (nand_2_out, CLK, SP_HIN);
  PowerSupply powersupply_1 (.VDD(VCC), .GND(GND));
  _74193 _74193_1 (
    .pin1(bussplitter_1_d1), .pin2(SP_INT[1]), .pin3(SP_INT[0]), .pin4(nDEC_SP), .pin5(nINC_SP),
    .pin6(SP_INT[2]), .pin7(SP_INT[3]), .pin8(GND), .pin9(bussplitter_1_d3), .pin10(bussplitter_1_d2),
    .pin11(nand_1_out), .pin12(_74193_1_pin12), .pin13(_74193_1_pin13), .pin14(RST),
    .pin15(bussplitter_1_d0), .pin16(VCC));
  _74193 _74193_2 (
    .pin1(bussplitter_1_d5), .pin2(SP_INT[5]), .pin3(SP_INT[4]), .pin4(_74193_1_pin13),
    .pin5(_74193_1_pin12), .pin6(SP_INT[6]), .pin7(SP_INT[7]), .pin8(GND), .pin9(bussplitter_1_d7),
    .pin10(bussplitter_1_d6), .pin11(nand_1_out), .pin12(_74193_2_pin12), .pin13(_74193_2_pin13),
    .pin14(RST), .pin15(bussplitter_1_d4), .pin16(VCC));
  _74193 _74193_3 (
    .pin1(bussplitter_1_d1), .pin2(SP_INT[9]), .pin3(SP_INT[8]), .pin4(_74193_2_pin13),
    .pin5(_74193_2_pin12), .pin6(SP_INT[10]), .pin7(SP_INT[11]), .pin8(GND), .pin9(bussplitter_1_d3),
    .pin10(bussplitter_1_d2), .pin11(nand_2_out), .pin12(_74193_3_pin12), .pin13(_74193_3_pin13),
    .pin14(RST), .pin15(bussplitter_1_d0), .pin16(VCC));
  _74193 _74193_4 (
    .pin1(bussplitter_1_d5), .pin2(SP_INT[13]), .pin3(SP_INT[12]), .pin4(_74193_3_pin13),
    .pin5(_74193_3_pin12), .pin6(SP_INT[14]), .pin7(SP_INT[15]), .pin8(GND), .pin9(bussplitter_1_d7),
    .pin10(bussplitter_1_d6), .pin11(nand_2_out), .pin14(RST), .pin15(bussplitter_1_d4), .pin16(VCC));  // open: pin12, pin13
  LED led_1 (.in(SP_INT[15]));
  LED led_2 (.in(SP_INT[14]));
  LED led_3 (.in(SP_INT[13]));
  LED led_4 (.in(SP_INT[12]));
  LED led_5 (.in(SP_INT[11]));
  LED led_6 (.in(SP_INT[10]));
  LED led_7 (.in(SP_INT[9]));
  LED led_8 (.in(SP_INT[8]));
  LED led_9 (.in(SP_INT[7]));
  LED led_10 (.in(SP_INT[6]));
  LED led_11 (.in(SP_INT[5]));
  LED led_12 (.in(SP_INT[4]));
  LED led_13 (.in(SP_INT[3]));
  LED led_14 (.in(SP_INT[2]));
  LED led_15 (.in(SP_INT[1]));
  LED led_16 (.in(SP_INT[0]));
  _74245 _74245_1 (
    .pin1(VCC), .pin2(SP_INT[0]), .pin3(SP_INT[1]), .pin4(SP_INT[2]), .pin5(SP_INT[3]), .pin6(SP_INT[4]),
    .pin7(SP_INT[5]), .pin8(SP_INT[6]), .pin9(SP_INT[7]), .pin10(GND), .pin11(_74245_1_pin11),
    .pin12(_74245_1_pin12), .pin13(_74245_1_pin13), .pin14(_74245_1_pin14), .pin15(_74245_1_pin15),
    .pin16(_74245_1_pin16), .pin17(_74245_1_pin17), .pin18(_74245_1_pin18), .pin19(nSP_OUT), .pin20(VCC));
  _74245 _74245_2 (
    .pin1(VCC), .pin2(SP_INT[8]), .pin3(SP_INT[9]), .pin4(SP_INT[10]), .pin5(SP_INT[11]), .pin6(SP_INT[12]),
    .pin7(SP_INT[13]), .pin8(SP_INT[14]), .pin9(SP_INT[15]), .pin10(GND), .pin11(_74245_2_pin11),
    .pin12(_74245_2_pin12), .pin13(_74245_2_pin13), .pin14(_74245_2_pin14), .pin15(_74245_2_pin15),
    .pin16(_74245_2_pin16), .pin17(_74245_2_pin17), .pin18(_74245_2_pin18), .pin19(nSP_OUT), .pin20(VCC));
  BusSplitter #(.Bits(16)) bussplitter_2 (
    .D(ADDR_BUS), .OE(GND), .D0(_74245_1_pin18), .D1(_74245_1_pin17), .D2(_74245_1_pin16),
    .D3(_74245_1_pin15), .D4(_74245_1_pin14), .D5(_74245_1_pin13), .D6(_74245_1_pin12), .D7(_74245_1_pin11),
    .D8(_74245_2_pin18), .D9(_74245_2_pin17), .D10(_74245_2_pin16), .D11(_74245_2_pin15),
    .D12(_74245_2_pin14), .D13(_74245_2_pin13), .D14(_74245_2_pin12), .D15(_74245_2_pin11));

  // Notes on the sheet:
  //   nDEC_SP: default 1
  //   VCC: default 1
  //   nSP_OUT: default 1
  //   nINC_SP: default 1
endmodule
